# Fritzing sketch smartcity (saved by Fritzing 0.9.4)
breadboards: 2

parts:
  M1 = DOIT Esp32 DevKit v1 (30 pins long, 11 pins width) [part_number=ESP32S-PIN30]
  LED1 = smd LED [color="Yellow (595nm)" package="0603 [SMD]"]
  LED2 = smd LED [color="Yellow (595nm)" package="0603 [SMD]"]
  LED3 = smd LED [color="Yellow (595nm)" package="0603 [SMD]"]
  LED4 = smd LED [color="Yellow (595nm)" package="0603 [SMD]"]
  R1 = Resistor [tolerance=±5% resistance=220 package=THT]
  R2 = Resistor [tolerance=±5% resistance=220 package=THT]
  R3 = Resistor [tolerance=±5% resistance=220 package=THT]
  R4 = Resistor [tolerance=±5% resistance=220 package=THT]
  M2 = DC Motor
  R5 = Photocell (LDR) [package=THT]
  M4 = fc-51 [package=THT]
  S1 = Pushbutton [package="[THT]"]
  S2 = Pushbutton [package="[THT]"]
  S3 = Pushbutton [package="[THT]"]
  S4 = Pushbutton [package="[THT]"]
  LED5 = LED - 5mm [color="Red (633nm)" package="5 mm [THT]"]
  LED6 = LED - 5mm [color="Red (633nm)" package="5 mm [THT]"]
  LED7 = LED - 5mm [color="Red (633nm)" package="5 mm [THT]"]
  LED8 = LED - 5mm [color="Red (633nm)" package="5 mm [THT]"]
  LED9 = LED - 5mm [color="Red (633nm)" package="5 mm [THT]"]
  LED10 = LED - 5mm [color="Red (633nm)" package="5 mm [THT]"]
  M5 = fc-51 [package=THT]
  R6 = Resistor [tolerance=±5% resistance=100 package=THT]
  R7 = Resistor [tolerance=±5% resistance=100 package=THT]
  R8 = Resistor [tolerance=±5% resistance=100 package=THT]
  R9 = Resistor [tolerance=±5% resistance=100 package=THT]
  R10 = Resistor [tolerance=±5% resistance=100 package=THT]
  R11 = Resistor [tolerance=±5% resistance=100 package=THT]
  S5 = Pushbutton [package="[THT]"]
  S6 = Pushbutton [package="[THT]"]
  R12 = Resistor [tolerance=±5% resistance=10k package=THT]
  U1 = Sharp PC817 [package=THT]
  LED11 = LED - 5mm [color="Yellow (595nm)" package="5 mm [THT]"]
  LED12 = LED - 5mm [color="Red (633nm)" package="5 mm [THT]"]
  LED13 = LED - 5mm [color="Green (570nm)" package="5 mm [THT]"]
  R13 = Resistor [tolerance=±5% resistance=100 package=THT]
  R14 = Resistor [tolerance=±5% resistance=100 package=THT]
  R15 = Resistor [tolerance=±5% resistance=100 package=THT]
  D1 = SOLAR-IXYS [package=solarbit-12x1]
  R16 = Resistor [tolerance=±5% resistance=220 package=THT]
  R17 = Resistor [tolerance=±5% resistance=10k package=THT]

nets:
  N1: M1.3V3, R5.pin_0, M4.pin3, M5.pin3, R17.Pin_1
  N2: M1.GND, R1.Pin_1, R2.Pin_1, R3.Pin_1, R4.Pin_1, M2.pin_1, M4.pin2, S1.Pin_1, S1.Pin_2, S2.Pin_1, S2.Pin_2, S3.Pin_1, S3.Pin_2, S4.Pin_1, S4.Pin_2, M5.pin2, R6.Pin_0, R7.Pin_0, R8.Pin_0, R9.Pin_0, R10.Pin_0, R11.Pin_0, S6.Pin_1, S6.Pin_2, R12.Pin_0, U1.Pin_3, R13.Pin_0, R14.Pin_0, R15.Pin_0
  N3: M1.D15, S6.Pin_3, S6.Pin_4
  N4: M1.D4, S1.Pin_3, S1.Pin_4
  N5: M1.RX2, S3.Pin_3, S3.Pin_4
  N6: M1.TX2, S4.Pin_3, S4.Pin_4
  N7: M1.D5, LED11.anode
  N8: M1.D18, LED1.anode, LED2.anode
  N9: M1.D19, LED3.anode, LED4.anode
  N10: M1.D23, LED12.anode
  N11: M1.VP, R5.pin_1, R12.Pin_1
  N12: M1.VN, U1.Pin_4, R17.Pin_0
  N13: M1.D34, M4.pin1
  N14: M1.D35, M5.pin1
  N15: M1.D32, LED7.anode
  N16: M1.D33, LED8.anode
  N17: M1.D25, S2.Pin_3, S2.Pin_4
  N18: M1.D26, LED5.anode, LED6.anode
  N19: M1.D27, LED9.anode
  N20: M1.D14, LED10.anode
  N21: M1.D13, LED13.anode
  N22: M1.VIN, S5.Pin_3, S5.Pin_4
  N23: LED1.cathode, R1.Pin_0
  N24: LED2.cathode, R2.Pin_0
  N25: LED3.cathode, R3.Pin_0
  N26: LED4.cathode, R4.Pin_0
  N27: M2.pin_2, S5.Pin_1, S5.Pin_2
  N28: LED5.cathode, R9.Pin_1
  N29: LED6.cathode, R8.Pin_1
  N30: LED7.cathode, R11.Pin_1
  N31: LED8.cathode, R10.Pin_1
  N32: LED9.cathode, R7.Pin_1
  N33: LED10.cathode, R6.Pin_1
  N34: U1.Pin_1, R16.Pin_0
  N35: U1.Pin_2, D1.C
  N36: LED11.cathode, R15.Pin_1
  N37: LED12.cathode, R14.Pin_1
  N38: LED13.cathode, R13.Pin_1
  N39: D1.A, R16.Pin_1

custom parts:
  DOIT Esp32 DevKit v1 (30 pins long, 11 pins width): The DOIT Esp32 DevKit v1 is one of the development board created by DOIT to evaluate the ESP-WROOM-32 module. It is based on the ESP32 microcontroller that boasts Wifi, Bluetooth, Ethernet and Low Power support all in a single chip. (vanepp) made breadboard work, adjusted pin numbering and labels and reduced size of schematic and cleaned up pcb. This chip is 30pins long (2 x15) and 11 pins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
